// Digital circuit GPR.dig as structural Verilog
module GPR (
  input  [1:0] Address,
  input  [3:0] Data,
  input  [1:0] Control,
  input  clk,
  output [3:0] out
);

  wire and_1_out, and_2_out, and_3_out, and_4_out, decoder_1_out_0, decoder_1_out_1, decoder_1_out_2,
       decoder_1_out_3;
  wire [3:0] R0_p4, R1_p4, R2_p4, R3_p4;

  Decoder #(.Selector_Bits(2)) decoder_1 (
    .sel(Address), .out_0(decoder_1_out_0), .out_1(decoder_1_out_1), .out_2(decoder_1_out_2),
    .out_3(decoder_1_out_3));
  and and_1 (and_1_out, decoder_1_out_0, clk);
  and and_2 (and_2_out, decoder_1_out_1, clk);
  and and_3 (and_3_out, decoder_1_out_2, clk);
  and and_4 (and_4_out, decoder_1_out_3, clk);
  // _4_bit_register2 R0: pin names not known; wires that end beside it: and_1_out, Data, Control, R0_p4
  // _4_bit_register2 R1: pin names not known; wires that end beside it: and_2_out, Data, Control, R1_p4
  // _4_bit_register2 R2: pin names not known; wires that end beside it: and_3_out, Data, Control, R2_p4
  // _4_bit_register2 R3: pin names not known; wires that end beside it: and_4_out, Data, Control, R3_p4
  Multiplexer #(.Selector_Bits(2), .Bits(4)) multiplexer_1 (
    .sel(Address), .in_0(R0_p4), .in_1(R1_p4), .in_2(R2_p4), .in_3(R3_p4), .out(out));
endmodule
