// Digital circuit hw1_full_adder.dig as structural Verilog
module hw1_full_adder (
  input  [3:0] A,
  input  [3:0] B,
  output Cout,
  output [3:0] Sum
);

  wire hw1_adder_1_cout, hw1_adder_2_cout, hw1_adder_3_cout;

  hw1_adder hw1_adder_1 (.A(A[0]), .B(B[0]), .Cin(1'b0), .Sum(Sum[0]), .Cout(hw1_adder_1_cout));
  hw1_adder hw1_adder_2 (.A(A[1]), .B(B[1]), .Cin(hw1_adder_1_cout), .Sum(Sum[1]), .Cout(hw1_adder_2_cout));
  hw1_adder hw1_adder_3 (.A(A[2]), .B(B[2]), .Cin(hw1_adder_2_cout), .Sum(Sum[2]), .Cout(hw1_adder_3_cout));
  hw1_adder hw1_adder_4 (.A(A[3]), .B(B[3]), .Cin(hw1_adder_3_cout), .Sum(Sum[3]), .Cout(Cout));
endmodule
